# Fritzing sketch circuit_Diagram_for_sensors (saved by Fritzing 0.8.5b)
breadboards: 1

parts:
  Part1 = Arduino Uno (Rev3)
  U1 = TMP36 [package=to-92-kit]
  R1 = PHOTOCELL [package=photocell-kit]
  U2 = QRD1114 [package=qrd1114]
  R2 = Resistor [tolerance=±5% resistance=1.8k package=THT]
  R3 = Resistor [tolerance=±5% resistance=10k package=THT]

nets:
  N1: Part1.A1, U1.VOUT, R2.Pin_0
  N2: Part1.A2, R1.P$2, R3.Pin_0
  N3: Part1.A3, U2.K
  N4: Part1.D8, R1.P$1
  N5: Part1.D9_PWM, U2.C
  GND: Part1.GND, U1.GND, U2.E, R3.Pin_1
  N6: Part1.D7, R2.Pin_1
